// Logisim project componentes_trabalho1.circ as structural Verilog
module Registrador_de_8_bits (
  input  [7:0] ENTRADA,
  input  CLOCK,
  output [7:0] SAIDA
);

  D_Flip_Flop d_ff_1 (.clk(CLOCK), .D(ENTRADA[7]), .Q(SAIDA[7]));  // open: Qn, preset, en, reset
  D_Flip_Flop d_ff_2 (.clk(CLOCK), .D(ENTRADA[6]), .Q(SAIDA[6]));  // open: Qn, preset, en, reset
  D_Flip_Flop d_ff_3 (.clk(CLOCK), .D(ENTRADA[5]), .Q(SAIDA[5]));  // open: Qn, preset, en, reset
  D_Flip_Flop d_ff_4 (.clk(CLOCK), .D(ENTRADA[4]), .Q(SAIDA[4]));  // open: Qn, preset, en, reset
  D_Flip_Flop d_ff_5 (.clk(CLOCK), .D(ENTRADA[3]), .Q(SAIDA[3]));  // open: Qn, preset, en, reset
  D_Flip_Flop d_ff_6 (.clk(CLOCK), .D(ENTRADA[2]), .Q(SAIDA[2]));  // open: Qn, preset, en, reset
  D_Flip_Flop d_ff_7 (.clk(CLOCK), .D(ENTRADA[1]), .Q(SAIDA[1]));  // open: Qn, preset, en, reset
  D_Flip_Flop d_ff_8 (.clk(CLOCK), .D(ENTRADA[0]), .Q(SAIDA[0]));  // open: Qn, preset, en, reset
endmodule

module Banco_de_registradores (
  input  [7:0] Dado_a_ser_escrito,
  input  Clear,
  input  Escrever_Reg,
  input  [2:0] Reg_a_ser_escrito,
  input  [2:0] Reg_a_ser_lido_1,
  input  [2:0] Reg_a_ser_lido_2,
  output [7:0] out_7,
  output [7:0] out_8
);

  wire clock_1_out, decoder_1_out0, decoder_1_out1, decoder_1_out2, decoder_1_out3, decoder_1_out4,
       decoder_1_out5, decoder_1_out6, decoder_1_out7;
  wire [7:0] register_1_q, register_2_q, register_3_q, register_4_q, register_5_q, register_6_q,
       register_7_q, register_8_q;

  Decoder #(.select(3)) decoder_1 (
    .out0(decoder_1_out0), .out1(decoder_1_out1), .out2(decoder_1_out2), .out3(decoder_1_out3),
    .out4(decoder_1_out4), .out5(decoder_1_out5), .out6(decoder_1_out6), .out7(decoder_1_out7),
    .sel(Reg_a_ser_escrito), .en(Escrever_Reg));
  Clock clock_1 (.out(clock_1_out));
  Register register_1 (.D(Dado_a_ser_escrito), .en(decoder_1_out0), .Q(register_1_q), .clk(clock_1_out), .clr(Clear));
  Register register_2 (.D(Dado_a_ser_escrito), .en(decoder_1_out1), .Q(register_2_q), .clk(clock_1_out), .clr(Clear));
  Register register_3 (.D(Dado_a_ser_escrito), .en(decoder_1_out2), .Q(register_3_q), .clk(clock_1_out), .clr(Clear));
  Register register_4 (.D(Dado_a_ser_escrito), .en(decoder_1_out3), .Q(register_4_q), .clk(clock_1_out), .clr(Clear));
  Register register_5 (.D(Dado_a_ser_escrito), .en(decoder_1_out4), .Q(register_5_q), .clk(clock_1_out), .clr(Clear));
  Register register_6 (.D(Dado_a_ser_escrito), .en(decoder_1_out5), .Q(register_6_q), .clk(clock_1_out), .clr(Clear));
  Register register_7 (.D(Dado_a_ser_escrito), .en(decoder_1_out6), .Q(register_7_q), .clk(clock_1_out), .clr(Clear));
  Register register_8 (.D(Dado_a_ser_escrito), .en(decoder_1_out7), .Q(register_8_q), .clk(clock_1_out), .clr(Clear));
  Multiplexer #(.select(3), .width(8)) multiplexer_1 (
    .in0(register_1_q), .in1(register_2_q), .in2(register_3_q), .in3(register_4_q), .in4(register_5_q),
    .in5(register_6_q), .in6(register_7_q), .in7(register_8_q), .out(out_7), .sel(Reg_a_ser_lido_1));  // open: en
  Multiplexer #(.select(3), .width(8)) multiplexer_2 (
    .in0(register_1_q), .in1(register_2_q), .in2(register_3_q), .in3(register_4_q), .in4(register_5_q),
    .in5(register_6_q), .in6(register_7_q), .in7(register_8_q), .out(out_8), .sel(Reg_a_ser_lido_2));  // open: en
endmodule

module ULA (
  input  [7:0] a0,
  input  [7:0] a1,
  input  [3:0] Seletor,
  input  [2:0] Shift_3bits,
  output [7:0] S,
  output Cout,
  output Cout_2
);

  wire [7:0] adder_1_out, and_1_out, nand_1_out, nor_1_out, or_1_out, shifter_1_out, shifter_2_out,
       subtractor_1_out, xor_1_out;

  Adder adder_1 (.a(a0), .b(a1), .out(adder_1_out), .cout(Cout));  // open: cin
  assign and_1_out = a0 & a1;  // AND_Gate and_1, 8 bits wide
  assign or_1_out = a0 | a1;  // OR_Gate or_1, 8 bits wide
  assign xor_1_out = a0 ^ a1;  // XOR_Gate xor_1, 8 bits wide
  assign nor_1_out = ~(a0 | a1);  // NOR_Gate nor_1, 8 bits wide
  assign nand_1_out = ~(a0 & a1);  // NAND_Gate nand_1, 8 bits wide
  Subtractor subtractor_1 (.a(a0), .b(a1), .out(subtractor_1_out), .bout(Cout_2));  // open: bin
  Shifter #(.shift("lr")) shifter_1 (.in(a0), .\dist (Shift_3bits), .out(shifter_1_out));
  Shifter shifter_2 (.in(a0), .\dist (Shift_3bits), .out(shifter_2_out));
  Multiplexer #(.select(4), .width(8), .enable("false")) multiplexer_1 (
    .in0(and_1_out), .in1(or_1_out), .in2(xor_1_out), .in3(nor_1_out), .in4(nand_1_out), .in5(shifter_1_out),
    .in6(shifter_2_out), .in7(adder_1_out), .in8(subtractor_1_out), .out(S), .sel(Seletor));  // open: in9, in10, in11, in12, in13, in14, in15

  // Notes on the sheet:
  //   0000
  //   0001
  //   0010
  //   0011
  //   0100
  //   0101
  //   0110
  //   0111
  //   1000
  //   1001
  //   Código do seletor
  //   AND
  //   OR
  //   NOT
  //   NOR
  //   NAND
  //   XOR
  //   SHIFT 3 bits a direita
  //   Somador
  //   Subtrador
  //   SHIFT 3 bits a esquerda
endmodule

module RAM_1x2 (
  input  [1:0] in_1,
  input  CLK,
  input  Ligar,
  input  Limpar,
  output [1:0] out_5
);

  wire j_k_ff_1_q, j_k_ff_2_q, not_1_out, not_2_out;

  not not_1 (not_1_out, in_1[1]);
  J_K_Flip_Flop j_k_ff_1 (
    .J(in_1[1]), .clk(CLK), .K(not_1_out), .Q(j_k_ff_1_q), .en(Ligar), .reset(Limpar));  // open: Qn, preset
  not not_2 (not_2_out, in_1[0]);
  J_K_Flip_Flop j_k_ff_2 (
    .J(in_1[0]), .clk(CLK), .K(not_2_out), .Q(j_k_ff_2_q), .en(Ligar), .reset(Limpar));  // open: Qn, preset
  and and_1 (out_5[0], Ligar, j_k_ff_2_q);
  and and_2 (out_5[1], Ligar, j_k_ff_1_q);
endmodule

module RAM_1x4 (
  input  clock,
  input  [3:0] Entrada,
  input  Ligar,
  input  Limpar,
  output [3:0] Saida
);

  RAM_1x2 ram_1x2_1 (.CLK(clock), .out_5(Saida[1:0]), .in_1(Entrada[1:0]), .Ligar(Ligar), .Limpar(Limpar));
  RAM_1x2 ram_1x2_2 (.CLK(clock), .out_5(Saida[3:2]), .in_1(Entrada[3:2]), .Ligar(Ligar), .Limpar(Limpar));
endmodule

module RAM_1x8 (
  input  CLOCK,
  input  [3:0] Entrada,
  input  [1:0] \Endereçamento ,
  input  Limpar,
  output [3:0] Saida
);

  wire chave_1_out_2, chave_1_out_3, chave_1_out_4, chave_1_out_5;
  wire [3:0] ram_1x4_1_saida, ram_1x4_2_saida, ram_1x4_3_saida, ram_1x4_4_saida;

  Chave chave_1 (
    .in_1(\Endereçamento ), .out_2(chave_1_out_2), .out_3(chave_1_out_3), .out_4(chave_1_out_4),
    .out_5(chave_1_out_5));
  RAM_1x4 ram_1x4_1 (.Entrada(Entrada), .Saida(ram_1x4_1_saida), .Ligar(chave_1_out_2), .Limpar(Limpar), .clock(CLOCK));
  RAM_1x4 ram_1x4_2 (.Entrada(Entrada), .Saida(ram_1x4_2_saida), .Ligar(chave_1_out_4), .Limpar(Limpar), .clock(CLOCK));
  RAM_1x4 ram_1x4_3 (.Entrada(Entrada), .Saida(ram_1x4_3_saida), .Ligar(chave_1_out_3), .Limpar(Limpar), .clock(CLOCK));
  RAM_1x4 ram_1x4_4 (.Entrada(Entrada), .Saida(ram_1x4_4_saida), .Ligar(chave_1_out_5), .Limpar(Limpar), .clock(CLOCK));
  assign Saida = ram_1x4_3_saida | ram_1x4_1_saida | ram_1x4_2_saida | ram_1x4_4_saida;  // OR_Gate or_1, 4 bits wide
endmodule

module Chave (
  input  [1:0] in_1,
  output out_2,
  output out_3,
  output out_4,
  output out_5
);

  wire not_1_out, not_2_out, not_3_out, not_4_out;

  not not_1 (not_1_out, in_1[0]);
  not not_2 (not_2_out, in_1[1]);
  not not_3 (not_3_out, in_1[1]);
  not not_4 (not_4_out, in_1[0]);
  and and_1 (out_2, not_1_out, not_2_out);
  and and_2 (out_3, in_1[0], not_3_out);
  and and_3 (out_4, in_1[1], not_4_out);
  and and_4 (out_5, in_1[1], in_1[0]);
endmodule

module RAM (
  input  CLOCK,
  input  [3:0] Entrada,
  input  [1:0] \Enderaçamento ,
  input  Limpar,
  output [3:0] Saida
);

  wire [1:0] undriven_2;
  wire [3:0] undriven;

  RAM_1x8 ram_1x8_1 (.Entrada(undriven), .\Endereçamento (undriven_2), .Saida(Saida), .Limpar(Limpar));  // open: CLOCK
endmodule

module Flip_Flop_D (
  input  CLOCK,
  input  D,
  input  in_3,
  input  in_4,
  input  Limpar,
  output Q,
  output nQ
);

  D_Flip_Flop d_ff_1 (.clk(CLOCK), .D(D), .Q(Q), .Qn(nQ), .preset(in_3), .en(in_4), .reset(Limpar));
endmodule

module Flip_Flop_JK (
  input  K,
  input  CLOCK,
  input  J,
  output Q,
  output nQ
);

  wire and_1_out, and_2_out;

  and and_1 (and_1_out, Q, K, CLOCK);
  and and_2 (and_2_out, CLOCK, J, nQ);
  nor nor_1 (Q, and_1_out, nQ);
  nor nor_2 (nQ, and_2_out, Q);
endmodule

module MUX_4x1 (
  input  A,
  input  B,
  input  C,
  input  D,
  input  Seletor1,
  input  Seletor2,
  output S
);

  wire and_1_out, and_2_out, and_3_out, and_4_out, not_1_out, not_2_out;

  not not_1 (not_1_out, Seletor1);
  not not_2 (not_2_out, Seletor2);
  and and_1 (and_1_out, A, Seletor1, Seletor2);
  and and_2 (and_2_out, B, not_1_out, Seletor2);
  and and_3 (and_3_out, C, not_2_out, Seletor1);
  and and_4 (and_4_out, D, not_1_out, not_2_out);
  or or_1 (S, and_1_out, and_2_out, and_3_out, and_4_out);

  // Notes on the sheet:
  //   Seletores 1 e 2
  //   Caso 00
  //   Caso 01
  //   Caso 10
  //   Caso 11
  //   Output
  //   D
  //   B
  //   C
  //   A
endmodule

module XOR (
  input  a0,
  input  a1,
  output S
);

  wire and_1_out, and_2_out, not_1_out, not_2_out;

  not not_1 (not_1_out, a0);
  not not_2 (not_2_out, a1);
  and and_1 (and_1_out, not_1_out, a1);
  and and_2 (and_2_out, a0, not_2_out);
  or or_1 (S, and_1_out, and_2_out);
endmodule

module Somador_8bits (
  input  a0,
  input  a1,
  input  a2,
  input  a3,
  input  a4,
  input  a5,
  input  a6,
  input  a7,
  input  a8,
  input  a9,
  input  a10,
  input  a11,
  input  a12,
  input  a13,
  input  a14,
  input  a15,
  output c0,
  output c1,
  output c2,
  output c3,
  output c4,
  output c5,
  output c6,
  output c7,
  output Cout
);

  wire base_do_somador_1_cout, base_do_somador_2_cout, base_do_somador_3_cout, base_do_somador_4_cout,
       base_do_somador_5_cout, base_do_somador_6_cout, base_do_somador_7_cout;

  base_do_somador base_do_somador_1 (.a0(a0), .a1(a1), .cin(1'b0), .S(c0), .cout(base_do_somador_1_cout));
  base_do_somador base_do_somador_2 (
    .a0(a2), .a1(a3), .cin(base_do_somador_1_cout), .S(c1), .cout(base_do_somador_2_cout));
  base_do_somador base_do_somador_3 (
    .a0(a4), .a1(a5), .cin(base_do_somador_2_cout), .S(c2), .cout(base_do_somador_3_cout));
  base_do_somador base_do_somador_4 (
    .a0(a6), .a1(a7), .cin(base_do_somador_3_cout), .S(c3), .cout(base_do_somador_4_cout));
  base_do_somador base_do_somador_5 (
    .a0(a8), .a1(a9), .cin(base_do_somador_4_cout), .S(c4), .cout(base_do_somador_5_cout));
  base_do_somador base_do_somador_6 (
    .a0(a10), .a1(a11), .cin(base_do_somador_5_cout), .S(c5), .cout(base_do_somador_6_cout));
  base_do_somador base_do_somador_7 (
    .a0(a12), .a1(a13), .cin(base_do_somador_6_cout), .S(c6), .cout(base_do_somador_7_cout));
  base_do_somador base_do_somador_8 (.a0(a14), .a1(a15), .cin(base_do_somador_7_cout), .S(c7), .cout(Cout));
endmodule

module Somador_4_bits (
  input  a0,
  input  b0,
  input  CarryIn,
  input  a1,
  input  b1,
  input  a2,
  input  b2,
  input  a3,
  input  b3,
  output c0,
  output c1,
  output c2,
  output c3,
  output cout
);

  wire base_do_somador_1_cout, base_do_somador_2_cout, base_do_somador_3_cout;

  base_do_somador base_do_somador_1 (.a0(a0), .a1(b0), .cin(CarryIn), .S(c0), .cout(base_do_somador_1_cout));
  base_do_somador base_do_somador_2 (
    .a0(a1), .a1(b1), .cin(base_do_somador_1_cout), .S(c1), .cout(base_do_somador_2_cout));
  base_do_somador base_do_somador_3 (
    .a0(a2), .a1(b2), .cin(base_do_somador_2_cout), .S(c2), .cout(base_do_somador_3_cout));
  base_do_somador base_do_somador_4 (.a0(a3), .a1(b3), .cin(base_do_somador_3_cout), .S(c3), .cout(cout));
endmodule

module base_do_somador (
  input  a0,
  input  a1,
  input  cin,
  output S,
  output cout
);

  wire and_1_out, and_2_out, and_3_out, xor_1_out;

  xor xor_1 (xor_1_out, a0, a1);
  and and_1 (and_1_out, a0, a1);
  and and_2 (and_2_out, a0, cin);
  and and_3 (and_3_out, a1, cin);
  xor xor_2 (S, xor_1_out, cin);
  or or_1 (cout, and_1_out, and_2_out, and_3_out);
endmodule

module extensor_de_sinal (
  input  [3:0] Entrada,
  output [7:0] \Saída 
);


  assign \Saída  = {4'b0000, Entrada};
endmodule

module Contador_Sincrono (
  input  in_1,
  input  in_2,
  input  in_3,
  input  in_4,
  input  in_5,
  input  in_6,
  input  in_7,
  input  in_8,
  output out_9,
  output out_10,
  output out_11,
  output out_12
);

  wire and_1_out, and_2_out, clock_1_out, nand_1_out, nand_2_out, nand_3_out, nand_4_out, nand_5_out,
       nand_6_out, nand_8_out, nand_9_out, nand_10_out, nand_11_out, nand_12_out, nand_13_out, nand_14_out,
       nand_16_out, nand_17_out, nand_18_out, nand_19_out, nand_20_out, nand_21_out, nand_22_out,
       nand_24_out, nand_25_out, nand_26_out, nand_27_out, nand_28_out, nand_29_out, nand_30_out,
       nand_32_out, not_1_out, not_2_out, not_3_out, not_4_out, not_5_out, not_6_out, not_7_out, not_8_out,
       not_9_out, not_10_out, not_11_out, not_12_out, not_13_out, not_14_out, not_15_out, not_16_out;

  Clock clock_1 (.out(clock_1_out));
  and and_1 (and_1_out, and_2_out, out_10);
  not not_1 (not_1_out, clock_1_out);
  not not_2 (not_2_out, in_1);
  nand nand_1 (nand_1_out, nand_8_out, and_1_out, not_1_out);
  nand nand_2 (nand_2_out, not_1_out, and_1_out, out_9);
  not not_3 (not_3_out, in_5);
  nand nand_3 (nand_3_out, not_2_out, nand_1_out, nand_4_out);
  not not_4 (not_4_out, not_1_out);
  nand nand_4 (nand_4_out, nand_3_out, nand_2_out, not_3_out);
  nand nand_5 (nand_5_out, nand_3_out, not_3_out, not_4_out);
  nand nand_6 (nand_6_out, not_4_out, not_2_out, nand_4_out);
  nand nand_7 (out_9, not_2_out, nand_5_out, nand_8_out);
  nand nand_8 (nand_8_out, out_9, nand_6_out, not_3_out);
  not not_5 (not_5_out, clock_1_out);
  not not_6 (not_6_out, in_2);
  nand nand_9 (nand_9_out, nand_16_out, and_2_out, not_5_out);
  nand nand_10 (nand_10_out, not_5_out, and_2_out, out_10);
  not not_7 (not_7_out, in_6);
  nand nand_11 (nand_11_out, not_6_out, nand_9_out, nand_12_out);
  not not_8 (not_8_out, not_5_out);
  nand nand_12 (nand_12_out, nand_11_out, nand_10_out, not_7_out);
  nand nand_13 (nand_13_out, nand_11_out, not_7_out, not_8_out);
  nand nand_14 (nand_14_out, not_8_out, not_6_out, nand_12_out);
  nand nand_15 (out_10, not_6_out, nand_13_out, nand_16_out);
  nand nand_16 (nand_16_out, out_10, nand_14_out, not_7_out);
  and and_2 (and_2_out, out_12, out_11);
  not not_9 (not_9_out, clock_1_out);
  not not_10 (not_10_out, in_3);
  nand nand_17 (nand_17_out, nand_24_out, out_12, not_9_out);
  nand nand_18 (nand_18_out, not_9_out, out_12, out_11);
  not not_11 (not_11_out, in_7);
  nand nand_19 (nand_19_out, not_10_out, nand_17_out, nand_20_out);
  not not_12 (not_12_out, not_9_out);
  nand nand_20 (nand_20_out, nand_19_out, nand_18_out, not_11_out);
  nand nand_21 (nand_21_out, nand_19_out, not_11_out, not_12_out);
  nand nand_22 (nand_22_out, not_12_out, not_10_out, nand_20_out);
  nand nand_23 (out_11, not_10_out, nand_21_out, nand_24_out);
  nand nand_24 (nand_24_out, out_11, nand_22_out, not_11_out);
  not not_13 (not_13_out, clock_1_out);
  not not_14 (not_14_out, in_4);
  nand nand_25 (nand_25_out, nand_32_out, 1'b1, not_13_out);
  nand nand_26 (nand_26_out, not_13_out, 1'b1, out_12);
  not not_15 (not_15_out, in_8);
  nand nand_27 (nand_27_out, not_14_out, nand_25_out, nand_28_out);
  not not_16 (not_16_out, not_13_out);
  nand nand_28 (nand_28_out, nand_27_out, nand_26_out, not_15_out);
  nand nand_29 (nand_29_out, nand_27_out, not_15_out, not_16_out);
  nand nand_30 (nand_30_out, not_16_out, not_14_out, nand_28_out);
  nand nand_31 (out_12, not_14_out, nand_29_out, nand_32_out);
  nand nand_32 (nand_32_out, out_12, nand_30_out, not_15_out);
endmodule

module UC (
  input  [2:0] in_1,
  output REGDEST,
  output ALU_Src,
  output Memto_Reg,
  output Reg_Write,
  output MemRead,
  output MemWrite,
  output Branch,
  output AluOp10,
  output AluOp01,
  output Jump
);

  Multiplexer #(.select(3), .width(10)) multiplexer_1 (
    .in0(10'h240), .in1(10'h1e6), .in2(10'h116), .in3(10'h146), .in4(10'ha), .in5(10'h1), .in6(10'h2c1),
    .in7(10'h144),
    .out({REGDEST, ALU_Src, Memto_Reg, Reg_Write, MemRead, MemWrite, Branch, AluOp10, AluOp01, Jump}),
    .sel(in_1));  // open: en

  // Notes on the sheet:
  //   000 - R-Type
  //   001 - LW
  //   010 - SW
  //   011 - ADDI
  //   100 - BEQ
  //   101 - J
  //   110 - JAL
  //   111 - SLTI
endmodule

module somador_8_bits_soma_4 (
  input  _7,
  input  _6,
  input  _5,
  input  _4,
  input  _3,
  input  _2,
  input  _1,
  input  _0,
  input  in_9,
  output Overflow
);

  wire adder_1_cout, adder_2_cout, adder_3_cout, adder_4_cout, adder_5_cout, adder_6_cout, adder_7_cout;
  wire [3:0] adder_1_out, adder_5_out;

  Adder #(.width(1)) adder_1 (.a(_0), .b(1'b0), .out(adder_1_out[0]), .cin(in_9), .cout(adder_1_cout));
  Adder #(.width(1)) adder_2 (.a(_1), .b(1'b0), .out(adder_1_out[1]), .cin(adder_1_cout), .cout(adder_2_cout));
  Adder #(.width(1)) adder_3 (.a(_2), .b(1'b1), .out(adder_1_out[2]), .cin(adder_2_cout), .cout(adder_3_cout));
  Adder #(.width(1)) adder_4 (.a(_3), .b(1'b0), .out(adder_1_out[3]), .cin(adder_3_cout), .cout(adder_4_cout));
  Adder #(.width(1)) adder_5 (.a(_4), .b(1'b0), .out(adder_5_out[0]), .cin(adder_4_cout), .cout(adder_5_cout));
  Adder #(.width(1)) adder_6 (.a(_5), .b(1'b0), .out(adder_5_out[1]), .cin(adder_5_cout), .cout(adder_6_cout));
  Adder #(.width(1)) adder_7 (.a(_6), .b(1'b0), .out(adder_5_out[2]), .cin(adder_6_cout), .cout(adder_7_cout));
  Adder #(.width(1)) adder_8 (.a(_7), .b(1'b0), .out(adder_5_out[3]), .cin(adder_7_cout), .cout(Overflow));
  Hex_Digit_Display hex_digit_display_1 (.value(adder_5_out));  // open: dp
  Hex_Digit_Display hex_digit_display_2 (.value(adder_1_out));  // open: dp
endmodule

module Somador_8_bits_real (
  input  a3,
  input  a2,
  input  a1,
  input  a0,
  input  b3,
  input  b2,
  input  b1,
  input  a0_2,
  input  CarryIn,
  input  a7,
  input  a6,
  input  a5,
  input  a4,
  input  b7,
  input  b6,
  input  b5,
  input  b4,
  output s0,
  output s1,
  output s2,
  output s3,
  output s4,
  output s5,
  output s6,
  output s7,
  output OVERFLOW
);

  wire somador_4_bits_1_cout;

  Somador_4_bits somador_4_bits_1 (
    .a0(a3), .b0(a2), .a1(a1), .b1(a0), .a2(b3), .b2(b2), .a3(b1), .b3(a0_2), .c0(s3), .c1(s2), .c2(s1),
    .c3(s0), .cout(somador_4_bits_1_cout), .CarryIn(CarryIn));
  Somador_4_bits somador_4_bits_2 (
    .a0(a7), .b0(a6), .a1(a5), .b1(a4), .a2(b7), .b2(b6), .a3(b5), .b3(b4), .c0(s7), .c1(s6), .c2(s5),
    .c3(s4), .cout(OVERFLOW), .CarryIn(somador_4_bits_1_cout));
endmodule
